// Logisim project Lab22.circ as structural Verilog: 3 circuits, main circuit main
module main (
  input  in_1,
  input  [7:0] Input_A,
  input  [7:0] Input_B,
  output [7:0] Output
);

  wire [7:0] xor_1_out;

  xor xor_1 (xor_1_out[0], in_1, Input_B[0]);
  xor xor_2 (xor_1_out[1], in_1, Input_B[1]);
  xor xor_3 (xor_1_out[2], in_1, Input_B[2]);
  xor xor_4 (xor_1_out[3], in_1, Input_B[3]);
  xor xor_5 (xor_1_out[4], in_1, Input_B[4]);
  xor xor_6 (xor_1_out[5], in_1, Input_B[5]);
  xor xor_7 (xor_1_out[6], in_1, Input_B[6]);
  xor xor_8 (xor_1_out[7], in_1, Input_B[7]);
  _8BitAdder u_8bitadder_1 (.in_1(in_1), .A_Input(Input_A), .B_Input(xor_1_out), .out_4(Output));

  // Notes on the sheet:
  //   A + B if 0 / A - B if 1
endmodule

module _1_bit_Adder (
  input  A,
  input  B,
  input  C,
  output S,
  output Cout
);

  wire and_1_out, and_2_out, and_3_out, and_4_out, and_5_out, and_6_out, and_7_out, not_1_out, not_2_out,
       not_3_out, or_1_out, or_2_out, xor_1_out, xor_2_out;

  not not_1 (not_1_out, A);
  not not_2 (not_2_out, B);
  not not_3 (not_3_out, C);
  xor xor_1 (xor_1_out, A, B);
  and and_1 (and_1_out, A, B);
  and and_2 (and_2_out, A, B);
  and and_3 (and_3_out, not_1_out, not_2_out);
  or or_1 (or_1_out, xor_1_out, and_1_out);
  or or_2 (or_2_out, and_2_out, and_3_out);
  xor xor_2 (xor_2_out, A, B);
  and and_4 (and_4_out, or_2_out, C);
  and and_5 (and_5_out, xor_2_out, not_3_out);
  and and_6 (and_6_out, C, or_1_out);
  and and_7 (and_7_out, A, B, not_3_out);
  or or_3 (Cout, and_6_out, and_7_out);
  or or_4 (S, and_4_out, and_5_out);
endmodule

module _8BitAdder (
  input  in_1,
  input  [7:0] A_Input,
  input  [7:0] B_Input,
  output [7:0] out_4
);

  wire n1_bit_adder_1_cout, n1_bit_adder_2_cout, n1_bit_adder_3_cout, n1_bit_adder_4_cout,
       n1_bit_adder_5_cout, n1_bit_adder_6_cout, n1_bit_adder_7_cout;

  _1_bit_Adder u_1_bit_adder_1 (.A(B_Input[0]), .B(A_Input[0]), .C(in_1), .S(out_4[0]), .Cout(n1_bit_adder_1_cout));
  _1_bit_Adder u_1_bit_adder_2 (
    .A(B_Input[1]), .B(A_Input[1]), .C(n1_bit_adder_1_cout), .S(out_4[1]), .Cout(n1_bit_adder_2_cout));
  _1_bit_Adder u_1_bit_adder_3 (
    .A(B_Input[2]), .B(A_Input[2]), .C(n1_bit_adder_2_cout), .S(out_4[2]), .Cout(n1_bit_adder_3_cout));
  _1_bit_Adder u_1_bit_adder_4 (
    .A(B_Input[3]), .B(A_Input[3]), .C(n1_bit_adder_3_cout), .S(out_4[3]), .Cout(n1_bit_adder_4_cout));
  _1_bit_Adder u_1_bit_adder_5 (
    .A(B_Input[4]), .B(A_Input[4]), .C(n1_bit_adder_4_cout), .S(out_4[4]), .Cout(n1_bit_adder_5_cout));
  _1_bit_Adder u_1_bit_adder_6 (
    .A(B_Input[5]), .B(A_Input[5]), .C(n1_bit_adder_5_cout), .S(out_4[5]), .Cout(n1_bit_adder_6_cout));
  _1_bit_Adder u_1_bit_adder_7 (
    .A(B_Input[6]), .B(A_Input[6]), .C(n1_bit_adder_6_cout), .S(out_4[6]), .Cout(n1_bit_adder_7_cout));
  _1_bit_Adder u_1_bit_adder_8 (.A(B_Input[7]), .B(A_Input[7]), .C(n1_bit_adder_7_cout), .S(out_4[7]));  // open: Cout
endmodule
