// Logisim project Lab21 (copy).circ as structural Verilog
module main (
  input  X,
  input  Y,
  output XXORY
);

  wire and_1_out, and_2_out, not_1_out, not_2_out;

  not not_1 (not_1_out, X);
  not not_2 (not_2_out, Y);
  and and_1 (and_1_out, not_1_out, Y);
  and and_2 (and_2_out, X, not_2_out);
  or or_1 (XXORY, and_1_out, and_2_out);

  // Notes on the sheet:
  //   XOR Circiut
endmodule
