// Logisim project lab23.circ as structural Verilog: 4 circuits, main circuit main
module main (
);

  wire button_1_out, button_2_out, button_3_out, button_4_out, button_5_out, button_6_out, comparator_1_lt,
       or_1_out, or_3_out;
  wire [7:0] and_1_out, and_2_out, and_3_out, and_4_out, and_5_out, bit_extender_1_out, bit_extender_2_out,
       bit_extender_3_out, bit_extender_4_out, bit_extender_5_out, n8_bit_adder_subtractor_1_output,
       n8_bit_adder_subtractor_2_output, or_2_out, register_1_q;

  Button button_1 (.out(button_1_out));
  Button button_2 (.out(button_2_out));
  Button button_3 (.out(button_3_out));
  Button button_4 (.out(button_4_out));
  Button button_5 (.out(button_5_out));
  Button button_6 (.out(button_6_out));
  or or_1 (or_1_out, button_5_out, button_4_out, button_3_out, button_2_out);
  assign bit_extender_1_out = {{7{button_2_out}}, button_2_out};  // Bit_Extender bit_extender_1
  assign bit_extender_2_out = {{7{button_3_out}}, button_3_out};  // Bit_Extender bit_extender_2
  assign bit_extender_3_out = {{7{button_4_out}}, button_4_out};  // Bit_Extender bit_extender_3
  assign bit_extender_4_out = {{7{button_5_out}}, button_5_out};  // Bit_Extender bit_extender_4
  assign bit_extender_5_out = {{7{button_6_out}}, button_6_out};  // Bit_Extender bit_extender_5
  assign and_1_out = 8'h1 & bit_extender_1_out;  // AND_Gate and_1, 8 bits wide
  assign and_2_out = 8'h2 & bit_extender_2_out;  // AND_Gate and_2, 8 bits wide
  assign and_3_out = 8'h5 & bit_extender_3_out;  // AND_Gate and_3, 8 bits wide
  assign and_4_out = 8'h14 & bit_extender_4_out;  // AND_Gate and_4, 8 bits wide
  assign and_5_out = 8'h14 & bit_extender_5_out;  // AND_Gate and_5, 8 bits wide
  assign or_2_out = and_1_out | and_2_out | and_3_out | and_4_out | and_5_out;  // OR_Gate or_2, 8 bits wide
  _8_bit_Adder_Subtractor u_8_bit_adder_subtractor_1 (
    .in_1(button_6_out), .Input_A(register_1_q), .Input_B(or_2_out), .Output(n8_bit_adder_subtractor_1_output));
  _8_bit_Adder_Subtractor u_8_bit_adder_subtractor_2 (
    .in_1(button_6_out), .Input_A(register_1_q), .Input_B(or_2_out), .Output(n8_bit_adder_subtractor_2_output));
  Comparator #(.mode("unsigned")) comparator_1 (
    .a(n8_bit_adder_subtractor_1_output), .b(8'h65), .lt(comparator_1_lt));  // open: gt, eq
  or or_3 (or_3_out, button_6_out, or_1_out);
  Register #(.trigger("falling")) register_1 (
    .D(n8_bit_adder_subtractor_2_output), .en(comparator_1_lt), .Q(register_1_q), .clk(or_3_out),
    .clr(button_1_out));
  Hex_Digit_Display hex_digit_display_1 (.value(register_1_q[7:4]));  // open: dp
  Hex_Digit_Display hex_digit_display_2 (.value(register_1_q[3:0]));  // open: dp

  // Notes on the sheet:
  //   Nickel
  //   Dime
  //   Quarter
  //   Dollar
  //   Reset Button
  //   Buy Something for a Dollar
endmodule

module _8_bit_Adder_Subtractor (
  input  in_1,
  input  [7:0] Input_A,
  input  [7:0] Input_B,
  output [7:0] Output
);

  wire [7:0] xor_1_out;

  xor xor_1 (xor_1_out[0], in_1, Input_B[0]);
  xor xor_2 (xor_1_out[1], in_1, Input_B[1]);
  xor xor_3 (xor_1_out[2], in_1, Input_B[2]);
  xor xor_4 (xor_1_out[3], in_1, Input_B[3]);
  xor xor_5 (xor_1_out[4], in_1, Input_B[4]);
  xor xor_6 (xor_1_out[5], in_1, Input_B[5]);
  xor xor_7 (xor_1_out[6], in_1, Input_B[6]);
  xor xor_8 (xor_1_out[7], in_1, Input_B[7]);
  _8_bit_Adder u_8_bit_adder_1 (.in_1(in_1), .A_Input(Input_A), .B_Input(xor_1_out), .out_4(Output));

  // Notes on the sheet:
  //   A + B if 0 / A - B if 1
endmodule

module _8_bit_Adder (
  input  in_1,
  input  [7:0] A_Input,
  input  [7:0] B_Input,
  output [7:0] out_4
);

  wire n1_bit_adder_1_cout, n1_bit_adder_2_cout, n1_bit_adder_3_cout, n1_bit_adder_4_cout,
       n1_bit_adder_5_cout, n1_bit_adder_6_cout, n1_bit_adder_7_cout;

  _1_bit_Adder u_1_bit_adder_1 (.A(B_Input[0]), .B(A_Input[0]), .C(in_1), .S(out_4[0]), .Cout(n1_bit_adder_1_cout));
  _1_bit_Adder u_1_bit_adder_2 (
    .A(B_Input[1]), .B(A_Input[1]), .C(n1_bit_adder_1_cout), .S(out_4[1]), .Cout(n1_bit_adder_2_cout));
  _1_bit_Adder u_1_bit_adder_3 (
    .A(B_Input[2]), .B(A_Input[2]), .C(n1_bit_adder_2_cout), .S(out_4[2]), .Cout(n1_bit_adder_3_cout));
  _1_bit_Adder u_1_bit_adder_4 (
    .A(B_Input[3]), .B(A_Input[3]), .C(n1_bit_adder_3_cout), .S(out_4[3]), .Cout(n1_bit_adder_4_cout));
  _1_bit_Adder u_1_bit_adder_5 (
    .A(B_Input[4]), .B(A_Input[4]), .C(n1_bit_adder_4_cout), .S(out_4[4]), .Cout(n1_bit_adder_5_cout));
  _1_bit_Adder u_1_bit_adder_6 (
    .A(B_Input[5]), .B(A_Input[5]), .C(n1_bit_adder_5_cout), .S(out_4[5]), .Cout(n1_bit_adder_6_cout));
  _1_bit_Adder u_1_bit_adder_7 (
    .A(B_Input[6]), .B(A_Input[6]), .C(n1_bit_adder_6_cout), .S(out_4[6]), .Cout(n1_bit_adder_7_cout));
  _1_bit_Adder u_1_bit_adder_8 (.A(B_Input[7]), .B(A_Input[7]), .C(n1_bit_adder_7_cout), .S(out_4[7]));  // open: Cout
endmodule

module _1_bit_Adder (
  input  A,
  input  B,
  input  C,
  output S,
  output Cout
);

  wire and_1_out, and_2_out, and_3_out, and_4_out, and_5_out, and_6_out, and_7_out, not_1_out, not_2_out,
       not_3_out, or_1_out, or_2_out, xor_1_out, xor_2_out;

  not not_1 (not_1_out, A);
  not not_2 (not_2_out, B);
  not not_3 (not_3_out, C);
  xor xor_1 (xor_1_out, A, B);
  and and_1 (and_1_out, A, B);
  and and_2 (and_2_out, A, B);
  and and_3 (and_3_out, not_1_out, not_2_out);
  or or_1 (or_1_out, xor_1_out, and_1_out);
  or or_2 (or_2_out, and_2_out, and_3_out);
  xor xor_2 (xor_2_out, A, B);
  and and_4 (and_4_out, or_2_out, C);
  and and_5 (and_5_out, xor_2_out, not_3_out);
  and and_6 (and_6_out, C, or_1_out);
  and and_7 (and_7_out, A, B, not_3_out);
  or or_3 (Cout, and_6_out, and_7_out);
  or or_4 (S, and_4_out, and_5_out);
endmodule
