// Logisim project lab24practice.circ as structural Verilog: 1 circuit, main circuit main
module main (
  input  [7:0] in_1,
  input  [7:0] in_2,
  input  in_3,
  output [7:0] out_4,
  output [7:0] out_5
);

  wire button_1_out, clock_1_out, comparator_1_eq;

  Clock clock_1 (.out(clock_1_out));
  Counter counter_1 (.Q(out_4), .clk(clock_1_out), .clr(button_1_out));  // open: load, D, count, carry
  Button button_1 (.out(button_1_out));
  Multiplexer #(.width(8)) multiplexer_1 (.in0(in_1), .in1(in_2), .out(out_5), .sel(in_3));  // open: en
  Comparator comparator_1 (.b(out_4), .eq(comparator_1_eq));  // open: a, gt, lt
endmodule
